# Fritzing sketch tanduino (saved by Fritzing 0.9.2b)
breadboards: 1

parts:
  Part1 = Arduino Pro Mini v13
  IC1 = Voltage Regulator [package=to220-5l]
  C1 = Electrolytic Capacitor [capacitance=1µF package="100 mil [THT, electrolytic]"]
  VCC1 = Battery block 9V
  GY-1 = GY-271 [part_number=GY-271]
  Part2 = Triple Axis Accelerometer Breakout - ADXL345
  LED1 = smd LED [color="Red (633nm)" package="0805 [SMD]"]
  R1 = Resistor [tolerance=±5% resistance=10k package="0603 [SMD]"]
  Nokia_5110_LCD_Module1 = Nokia 5110 LCD basado en PCD8544
  S1 = Round Pushbutton
  R3 = Resistor [tolerance=±5% resistance=10k package="0603 [SMD]"]
  R4 = Trimmer Potentiometer [maximum_resistance=10kΩ package=THT]
  U1 = SWITCH-SPST-2 [package=r_sw_th]
  C2 = Capacitor [part_number=100nF package=cap-pth-small2]

nets:
  N1: Part1.A4, GY-1.SDA, Part2.SDA
  N2: Part1.A5, GY-1.SCL, Part2.SCL
  GND: Part1.GND, IC1.GND, C1.-, VCC1.-, GY-1.GND, Part2.GND, R1.Pin_1, Nokia_5110_LCD_Module1.GND, S1.leg1, R4.leg1, C2.2
  VCC: Part1.VCC, Part1.A0, IC1.OUT, IC1.SENSE, C1.+, GY-1.VCC, Part2.VCC, Nokia_5110_LCD_Module1.VCC
  N3: Part1.A1, IC1.IN, U1.P
  N4: Part1.D12/MISO, Part1.D8, Nokia_5110_LCD_Module1.DC
  N5: Part1.D11_PWM/MOSI, Nokia_5110_LCD_Module1.DIN
  N6: Part1.D10_PWM/SS, Nokia_5110_LCD_Module1.CE
  N7: Part1.D9_PWM, Nokia_5110_LCD_Module1.RST
  N8: Part1.D7, LED1.anode
  N9: Part1.D2, R3.Pin_1
  N10: VCC1.+, U1.O
  N11: LED1.cathode, R1.Pin_0
  N12: Nokia_5110_LCD_Module1.LIGHT, R4.wiper
  N13: S1.leg0, R3.Pin_0, C2.1

custom parts:
  Voltage Regulator: Voltage Regulator LT1529
  GY-271: GY-271 - Electronic compass module - 3 Axis Magnetic Field Sensor HMC5883L
  Nokia 5110 LCD basado en PCD8544: Módulo Nokia 5110 LCD basado en el controlador PCD8544. Versión de 8 pines (sólo entrada).
